// Logisim project cpu.circ as structural Verilog: 4 circuits, main circuit main
module main (
  output [8:0] out_1,
  output [8:0] out_2,
  output [8:0] out_3,
  output [8:0] out_4,
  output [8:0] out_5,
  output [8:0] out_6,
  output [8:0] out_7,
  output [8:0] out_8,
  output [8:0] out_9,
  output [8:0] out_10
);

  wire ADD, ADDI, AND, clock_1_out, clock_2_out, comparator_1_lt, counter_1_carry, decoder_1_out0,
       decoder_1_out1, decoder_1_out2, decoder_1_out3, decoder_1_out4, decoder_1_out5, decoder_1_out6, Halt,
       MOV, MOVI, NOP, nor_1_out, NOT, not_1_out, OR, or_1_out, Reset, SLL, SRL, SUB, SUBI, TClock;
  wire [2:0] A, B, D, multiplexer_3_out, rom_1_data;
  wire [3:0] multiplexer_4_out;
  wire [4:0] counter_1_q, MSB, pc_1_output;
  wire [6:0] adder_1_out, LSB;
  wire [8:0] Data;
  wire [21:18] ram_1_data;

  Clock clock_1 (.out(clock_1_out));
  Decoder #(.select(3)) decoder_1 (
    .out0(decoder_1_out0), .out1(decoder_1_out1), .out2(decoder_1_out2), .out3(decoder_1_out3),
    .out4(decoder_1_out4), .out5(decoder_1_out5), .out6(decoder_1_out6), .sel(D), .en(nor_1_out));  // open: out7
  nor nor_1 (nor_1_out, Halt, NOP);
  PC pc_1 (.Clock(clock_1_out), .Halt(Halt), .Output(pc_1_output));
  Register register_1 (.Clock(clock_1_out), .Enable(decoder_1_out0), .Output(out_1), .Input(out_10));
  Register register_2 (.Clock(clock_1_out), .Enable(decoder_1_out1), .Output(out_2), .Input(out_10));
  Register register_3 (.Clock(clock_1_out), .Enable(decoder_1_out2), .Output(out_3), .Input(out_10));
  Register register_4 (.Clock(clock_1_out), .Enable(decoder_1_out3), .Output(out_4), .Input(out_10));
  Register register_5 (.Clock(clock_1_out), .Enable(decoder_1_out4), .Output(out_5), .Input(out_10));
  Register register_6 (.Clock(clock_1_out), .Enable(decoder_1_out5), .Output(out_6), .Input(out_10));
  Register register_7 (.Clock(clock_1_out), .Enable(decoder_1_out6), .Output(out_7), .Input(out_10));
  RAM #(.addrWidth(5), .dataWidth(22)) ram_1 (
    .addr(pc_1_output), .data({ram_1_data, A, B, D, Data}));  // open: sel, clk, ld, clr
  Decoder #(.select(4)) decoder_2 (
    .out0(AND), .out1(OR), .out2(NOT), .out3(ADD), .out4(MOV), .out5(SLL), .out6(SRL), .out7(SUB),
    .out8(ADDI), .out9(SUBI), .out10(MOVI), .out11(NOP), .out15(Halt), .sel(ram_1_data));  // open: out12, out13, out14, en
  Multiplexer #(.select(3), .width(9)) multiplexer_1 (
    .in0(out_1), .in1(out_2), .in2(out_3), .in3(out_4), .in4(out_5), .in5(out_6), .in6(out_7), .out(out_9),
    .sel(A));  // open: in7, en
  ALU alu_1 (.RA(out_9), .RB(out_8), .OPCODE(ram_1_data), .Output(out_10));
  Multiplexer #(.select(3), .width(9)) multiplexer_2 (
    .in0(out_1), .in1(out_2), .in2(out_3), .in3(out_4), .in4(out_5), .in5(out_6), .in6(out_7), .in7(Data),
    .out(out_8), .sel(multiplexer_3_out));  // open: en
  Multiplexer #(.width(3)) multiplexer_3 (.in0(B), .in1(3'b111), .out(multiplexer_3_out), .sel(or_1_out));  // open: en
  or or_1 (or_1_out, MOVI, SUBI, ADDI);
  TTY #(.rows(33), .cols(1)) tty_1 (.data({2'b10, MSB}), .clk(TClock), .clr(Reset));  // open: we
  TTY #(.rows(33), .cols(1)) tty_2 (.data(LSB), .clk(TClock), .clr(Reset));  // open: we
  Button u_Reset (.out(Reset));
  Counter #(.width(5), .max('h1f), .ongoal("stay")) counter_1 (
    .Q(counter_1_q), .carry(counter_1_carry), .clk(TClock), .clr(Reset));  // open: load, D, count
  Multiplexer #(.select(3), .width(9), .disabled(0), .enable("false")) multiplexer_4 (
    .in0(out_1), .in1(out_2), .in2(out_3), .in3(out_4), .in4(out_5), .in5(out_6), .in6(out_7),
    .out({MSB, multiplexer_4_out}), .sel(rom_1_data));  // open: in7
  not not_1 (not_1_out, counter_1_carry);
  Clock clock_2 (.out(clock_2_out));
  ROM #(.addrWidth(5), .dataWidth(3)) rom_1 (.addr(counter_1_q), .data(rom_1_data));  // open: sel
  and and_1 (TClock, not_1_out, clock_2_out);
  // Probe on {3'b011, multiplexer_4_out}
  Comparator #(.width(7)) comparator_1 (
    .a(7'b0111001), .b({3'b011, multiplexer_4_out}), .lt(comparator_1_lt));  // open: gt, eq
  // Probe on {2'b10, MSB}
  Adder #(.width(7)) adder_1 (.a({3'b011, multiplexer_4_out}), .b(7'b0000111), .out(adder_1_out));  // open: cin, cout
  // Probe on LSB
  Multiplexer #(.width(7), .disabled(0), .enable("false")) multiplexer_5 (
    .in0({3'b011, multiplexer_4_out}), .in1(adder_1_out), .out(LSB), .sel(comparator_1_lt));

  // Other names for the same wires on the sheet: R0[8:0] = out_1; R1[8:0] = out_2; R2[8:0] = out_3; R3[8:0] = out_4;
  //   R4[8:0] = out_5; R5[8:0] = out_6; R6[8:0] = out_7; Rn[8:0] = out_10

  // Notes on the sheet:
  //   @0
  //   JA
  //   E5
  //   @0
  //   OF
  //   U5
  //   OF
  //   E5
  //   E5
  //   U4
  //   E5
  //   E5
  //   U4
  //   _F
  //   _F
  //   _F
  //   AF
  //   AF
  //   AF
  //   @0
  //   AE
  //   AE
  //   AE
  //   _E
  //   OF
  //   ^0
  //   J9
  //   P1
  //   R0
  //   R0
  //   _F
  //   contents of rom_1 (hex, n*v repeats v):
  //   0 0 1 2 3 4 5 6 6 2 3 4 5 6 6 0 1 2 3 4 5 6 6 2 3 4 5 6 6 6
endmodule

module Register (
  input  Clock,
  input  Enable,
  input  [8:0] Input,
  output [8:0] Output
);

  D_Flip_Flop d_ff_1 (.clk(Clock), .D(Input[8]), .Q(Output[8]), .en(Enable));  // open: Qn, preset, reset
  D_Flip_Flop d_ff_2 (.clk(Clock), .D(Input[7]), .Q(Output[7]), .en(Enable));  // open: Qn, preset, reset
  D_Flip_Flop d_ff_3 (.clk(Clock), .D(Input[6]), .Q(Output[6]), .en(Enable));  // open: Qn, preset, reset
  D_Flip_Flop d_ff_4 (.clk(Clock), .D(Input[5]), .Q(Output[5]), .en(Enable));  // open: Qn, preset, reset
  D_Flip_Flop d_ff_5 (.clk(Clock), .D(Input[4]), .Q(Output[4]), .en(Enable));  // open: Qn, preset, reset
  D_Flip_Flop d_ff_6 (.clk(Clock), .D(Input[3]), .Q(Output[3]), .en(Enable));  // open: Qn, preset, reset
  D_Flip_Flop d_ff_7 (.clk(Clock), .D(Input[2]), .Q(Output[2]), .en(Enable));  // open: Qn, preset, reset
  D_Flip_Flop d_ff_8 (.clk(Clock), .D(Input[1]), .Q(Output[1]), .en(Enable));  // open: Qn, preset, reset
  D_Flip_Flop d_ff_9 (.clk(Clock), .D(Input[0]), .Q(Output[0]), .en(Enable));  // open: Qn, preset, reset
endmodule

module PC (
  input  Clock,
  input  Halt,
  output [4:0] Output
);

  wire and_1_out, not_1_out, t_ff_1_qn, t_ff_2_qn, t_ff_3_qn, t_ff_4_qn;

  not not_1 (not_1_out, Halt);
  and and_1 (and_1_out, Clock, not_1_out);
  T_Flip_Flop t_ff_1 (.clk(and_1_out), .T(1'b1), .Q(Output[0]), .Qn(t_ff_1_qn));  // open: preset, reset, en
  T_Flip_Flop t_ff_2 (.clk(t_ff_1_qn), .T(1'b1), .Q(Output[1]), .Qn(t_ff_2_qn));  // open: preset, reset, en
  T_Flip_Flop t_ff_3 (.clk(t_ff_2_qn), .T(1'b1), .Q(Output[2]), .Qn(t_ff_3_qn));  // open: preset, reset, en
  T_Flip_Flop t_ff_4 (.clk(t_ff_3_qn), .T(1'b1), .Q(Output[3]), .Qn(t_ff_4_qn));  // open: preset, reset, en
  T_Flip_Flop t_ff_5 (.clk(t_ff_4_qn), .T(1'b1), .Q(Output[4]));  // open: Qn, preset, reset, en
endmodule

module ALU (
  input  [3:0] OPCODE,
  input  [8:0] RA,
  input  [8:0] RB,
  output [8:0] Output
);

  wire and_2_out, and_3_out, and_4_out, and_5_out, and_6_out, and_7_out, and_8_out, and_9_out, and_10_out,
       and_11_out, and_12_out, and_13_out, and_14_out, and_15_out, and_16_out, and_17_out, and_18_out,
       and_19_out, B0, B1, B2, B3, B4, B5, B6, B7, B8, C1, C2, C3, C4, C5, C6, C7, C8, C9, decoder_1_out7,
       decoder_1_out9, not_2_out, not_3_out, not_4_out, not_5_out, not_6_out, not_7_out, not_8_out,
       not_9_out, not_10_out, or_2_out, xor_1_out, xor_3_out, xor_5_out, xor_7_out, xor_9_out, xor_11_out,
       xor_13_out, xor_15_out, xor_17_out;
  wire [8:0] Adder, AND_out, not_1_out, OR_out;

  assign AND_out = RA & RB;  // AND_Gate AND, 9 bits wide
  assign OR_out = RA | RB;  // OR_Gate OR, 9 bits wide
  Multiplexer #(.select(4), .width(9)) multiplexer_1 (
    .in0(AND_out), .in1(OR_out), .in2(not_1_out), .in3(Adder), .in4(RA), .in5({RA[7:0], 1'b0}),
    .in6({1'b0, RA[8:1]}), .in7(Adder), .in8(Adder), .in9(Adder), .in10(RB), .out(Output), .sel(OPCODE));  // open: in11, in12, in13, in14, in15, en
  assign not_1_out = ~RA;  // NOT_Gate not_1, 9 bits wide
  Decoder #(.select(4)) decoder_1 (
    .out7(decoder_1_out7), .out9(decoder_1_out9), .sel(OPCODE));  // open: out0, out1, out2, out3, out4, out5, out6, out8, out10, out11, out12, out13, out14, out15, en
  or or_2 (or_2_out, decoder_1_out7, decoder_1_out9);
  Multiplexer multiplexer_2 (.in0(RB[8]), .in1(not_2_out), .out(B8), .sel(or_2_out));  // open: en
  not not_2 (not_2_out, RB[8]);
  Multiplexer multiplexer_3 (.in0(RB[7]), .in1(not_3_out), .out(B7), .sel(or_2_out));  // open: en
  not not_3 (not_3_out, RB[7]);
  Multiplexer multiplexer_4 (.in0(RB[6]), .in1(not_4_out), .out(B6), .sel(or_2_out));  // open: en
  not not_4 (not_4_out, RB[6]);
  Multiplexer multiplexer_5 (.in0(RB[5]), .in1(not_5_out), .out(B5), .sel(or_2_out));  // open: en
  not not_5 (not_5_out, RB[5]);
  Multiplexer multiplexer_6 (.in0(RB[4]), .in1(not_6_out), .out(B4), .sel(or_2_out));  // open: en
  not not_6 (not_6_out, RB[4]);
  Multiplexer multiplexer_7 (.in0(RB[3]), .in1(not_7_out), .out(B3), .sel(or_2_out));  // open: en
  not not_7 (not_7_out, RB[3]);
  Multiplexer multiplexer_8 (.in0(RB[2]), .in1(not_8_out), .out(B2), .sel(or_2_out));  // open: en
  not not_8 (not_8_out, RB[2]);
  Multiplexer multiplexer_9 (.in0(RB[1]), .in1(not_9_out), .out(B1), .sel(or_2_out));  // open: en
  not not_9 (not_9_out, RB[1]);
  Multiplexer multiplexer_10 (.in0(RB[0]), .in1(not_10_out), .out(B0), .sel(or_2_out));  // open: en
  not not_10 (not_10_out, RB[0]);
  xor xor_1 (xor_1_out, B0, RA[0]);
  and and_2 (and_2_out, B0, RA[0]);
  or or_3 (C1, and_2_out, and_3_out);
  and and_3 (and_3_out, or_2_out, xor_1_out);
  xor xor_2 (Adder[0], or_2_out, xor_1_out);
  and and_4 (and_4_out, B1, RA[1]);
  or or_4 (C2, and_4_out, and_5_out);
  xor xor_3 (xor_3_out, B1, RA[1]);
  and and_5 (and_5_out, C1, xor_3_out);
  xor xor_4 (Adder[1], C1, xor_3_out);
  and and_6 (and_6_out, B2, RA[2]);
  or or_5 (C3, and_6_out, and_7_out);
  xor xor_5 (xor_5_out, B2, RA[2]);
  and and_7 (and_7_out, C2, xor_5_out);
  xor xor_6 (Adder[2], C2, xor_5_out);
  and and_8 (and_8_out, B3, RA[3]);
  or or_6 (C4, and_8_out, and_9_out);
  xor xor_7 (xor_7_out, B3, RA[3]);
  and and_9 (and_9_out, C3, xor_7_out);
  xor xor_8 (Adder[3], C3, xor_7_out);
  and and_10 (and_10_out, B4, RA[4]);
  or or_7 (C5, and_10_out, and_11_out);
  xor xor_9 (xor_9_out, B4, RA[4]);
  and and_11 (and_11_out, C4, xor_9_out);
  xor xor_10 (Adder[4], C4, xor_9_out);
  or or_8 (C6, and_12_out, and_13_out);
  xor xor_11 (xor_11_out, B5, RA[5]);
  and and_12 (and_12_out, B5, RA[5]);
  and and_13 (and_13_out, C5, xor_11_out);
  xor xor_12 (Adder[5], C5, xor_11_out);
  and and_14 (and_14_out, B6, RA[6]);
  or or_9 (C7, and_14_out, and_15_out);
  xor xor_13 (xor_13_out, B6, RA[6]);
  and and_15 (and_15_out, C6, xor_13_out);
  xor xor_14 (Adder[6], C6, xor_13_out);
  and and_16 (and_16_out, B7, RA[7]);
  or or_10 (C8, and_16_out, and_17_out);
  xor xor_15 (xor_15_out, B7, RA[7]);
  and and_17 (and_17_out, C7, xor_15_out);
  xor xor_16 (Adder[7], C7, xor_15_out);
  and and_18 (and_18_out, B8, RA[8]);
  or or_11 (C9, and_18_out, and_19_out);
  xor xor_17 (xor_17_out, B8, RA[8]);
  and and_19 (and_19_out, C8, xor_17_out);
  xor xor_18 (Adder[8], C8, xor_17_out);

  // Other names for the same wires on the sheet: S0 = Adder[0]; S1 = Adder[1]; S2 = Adder[2]; S3 = Adder[3];
  //   S4 = Adder[4]; S5 = Adder[5]; S6 = Adder[6]; S7 = Adder[7]; S8 = Adder[8]; A0 = RA[0]; A1 = RA[1]; A2 = RA[2];
  //   A3 = RA[3]; A4 = RA[4]; A5 = RA[5]; A6 = RA[6]; A7 = RA[7]; A8 = RA[8]
endmodule
